# Fritzing sketch remote sketch (saved by Fritzing 0.9.3b)
breadboards: 1

parts:
  Part1 = Photon
  WeMos_D1_Mini_OLED_Shield1 = WeMos D1 Mini OLED Shield  # not connected
  S1 = Momentary Switch [package=ksa_sealed_tac_switch]
  S2 = Momentary Switch [package=ksa_sealed_tac_switch]

nets:
  N1: Part1.GND, S1.4, S2.4
  N2: Part1.D3, S2.2
  N3: Part1.D4, S1.2
