# Fritzing sketch sketch (saved by Fritzing 0.9.3b)
breadboards: 1

parts:
  Part1 = Photon
  S1 = Pushbutton [package="[THT]"]
  S2 = Pushbutton [package="[THT]"]
  S3 = Pushbutton [package="[THT]"]
  LED1 = LED - 5mm [color="Red (633nm)" package="5 mm [THT]"]  # not connected
  S4 = SPST Switch [package=switch-spdt_kit]
  LED2 = LED - 5mm [color="Red (633nm)" package="5 mm [THT]"]  # not connected
  LED3 = LED - 5mm [color="Yellow (595nm)" package="5 mm [THT]"]
  LED4 = LED - 5mm [color="Green (570nm)" package="5 mm [THT]"]
  R1 = Resistor [tolerance=±5% resistance=220 package=THT]
  R2 = Resistor [tolerance=±5% resistance=220 package=THT]
  R3 = Resistor [tolerance=±5% resistance=220 package=THT]

nets:
  N1: Part1.D1, LED3.anode
  N2: Part1.D2, LED4.anode
  N3: Part1.D3, S4.P
  N4: Part1.D4, S1.Pin_3, S1.Pin_4
  N5: Part1.D5, S2.Pin_3, S2.Pin_4
  N6: Part1.D6, S3.Pin_3, S3.Pin_4
  N7: S1.Pin_1, S1.Pin_2
  N8: S2.Pin_1, S2.Pin_2
  N9: S3.Pin_1, S3.Pin_2, S4.O, R2.Pin_0, R3.Pin_0
  N10: LED3.cathode, R1.Pin_1
